// Logisim project cpu_01.circ as structural Verilog: 3 circuits, main circuit FullAdder_1bit
module FullAdder_1bit (
  input  Ain,
  input  Bin,
  input  CarryIn,
  output Sum,
  output CarryOut
);

  wire and_1_out, and_2_out, xor_1_out;

  xor xor_1 (xor_1_out, Ain, Bin);
  xor xor_2 (Sum, xor_1_out, CarryIn);
  and and_1 (and_1_out, CarryIn, xor_1_out);
  and and_2 (and_2_out, Bin, Ain);
  or or_1 (CarryOut, and_1_out, and_2_out);
endmodule

module FullAdder_8bit (
  input  CarryIn,
  input  [7:0] Ain,
  input  [7:0] Bin,
  output [7:0] Sum,
  output CarryOut
);

  wire fulladder_1bit_1_carryout, fulladder_1bit_2_carryout, fulladder_1bit_3_carryout,
       fulladder_1bit_4_carryout, fulladder_1bit_5_carryout, fulladder_1bit_6_carryout,
       fulladder_1bit_7_carryout;

  FullAdder_1bit fulladder_1bit_1 (
    .Ain(Ain[0]), .Bin(Bin[0]), .CarryIn(CarryIn), .Sum(Sum[0]), .CarryOut(fulladder_1bit_1_carryout));
  FullAdder_1bit fulladder_1bit_2 (
    .Ain(Ain[1]), .Bin(Bin[1]), .CarryIn(fulladder_1bit_1_carryout), .Sum(Sum[1]),
    .CarryOut(fulladder_1bit_2_carryout));
  FullAdder_1bit fulladder_1bit_3 (
    .Ain(Ain[2]), .Bin(Bin[2]), .CarryIn(fulladder_1bit_2_carryout), .Sum(Sum[2]),
    .CarryOut(fulladder_1bit_3_carryout));
  FullAdder_1bit fulladder_1bit_4 (
    .Ain(Ain[3]), .Bin(Bin[3]), .CarryIn(fulladder_1bit_3_carryout), .Sum(Sum[3]),
    .CarryOut(fulladder_1bit_4_carryout));
  FullAdder_1bit fulladder_1bit_5 (
    .Ain(Ain[4]), .Bin(Bin[4]), .CarryIn(fulladder_1bit_4_carryout), .Sum(Sum[4]),
    .CarryOut(fulladder_1bit_5_carryout));
  FullAdder_1bit fulladder_1bit_6 (
    .Ain(Ain[5]), .Bin(Bin[5]), .CarryIn(fulladder_1bit_5_carryout), .Sum(Sum[5]),
    .CarryOut(fulladder_1bit_6_carryout));
  FullAdder_1bit fulladder_1bit_7 (
    .Ain(Ain[6]), .Bin(Bin[6]), .CarryIn(fulladder_1bit_6_carryout), .Sum(Sum[6]),
    .CarryOut(fulladder_1bit_7_carryout));
  FullAdder_1bit fulladder_1bit_8 (
    .Ain(Ain[7]), .Bin(Bin[7]), .CarryIn(fulladder_1bit_7_carryout), .Sum(Sum[7]), .CarryOut(CarryOut));
endmodule

module ALU (
  input  [7:0] in_1,
  input  [7:0] in_2,
  output [7:0] out_3,
  output out_4
);

  FullAdder_8bit fulladder_8bit_1 (.Bin(in_2), .CarryIn(1'b0), .Ain(in_1), .Sum(out_3), .CarryOut(out_4));
endmodule
