// Logisim project cpu_v0.2.circ as structural Verilog: 2 circuits, main circuit ALU
module ALU (
  input  [3:0] Cmd,
  input  CarryIn,
  input  [7:0] Ain,
  input  [7:0] Bin,
  output [7:0] Sum,
  output [7:0] Flags
);

  wire adder_1_cout, and_1_out, and_2_out, and_3_out, not_1_out, subtractor_1_bout;
  wire [7:0] adder_1_out, and_4_out, multiplexer_1_out, negator_1_out, not_2_out, not_3_out, or_1_out,
       shifter_1_out, shifter_2_out, subtractor_1_out, xor_1_out;

  and and_1 (and_1_out, Cmd[1], not_1_out, Cmd[3]);
  Multiplexer #(.width(8)) multiplexer_1 (.in0(Bin), .in1(8'h1), .out(multiplexer_1_out), .sel(and_1_out));
  not not_1 (not_1_out, Cmd[2]);
  and and_2 (and_2_out, Cmd[1], Cmd[2], Cmd[3]);
  and and_3 (and_3_out, and_2_out, CarryIn);
  Adder adder_1 (.a(Ain), .b(multiplexer_1_out), .out(adder_1_out), .cin(and_3_out), .cout(adder_1_cout));
  Subtractor subtractor_1 (
    .a(Ain), .b(multiplexer_1_out), .out(subtractor_1_out), .bin(and_3_out), .bout(subtractor_1_bout));
  Negator negator_1 (.in(Ain), .out(negator_1_out));
  Shifter shifter_1 (.in(Ain), .\dist (multiplexer_1_out[2:0]), .out(shifter_1_out));
  Shifter #(.shift("lr")) shifter_2 (.in(Ain), .\dist (multiplexer_1_out[2:0]), .out(shifter_2_out));
  assign and_4_out = Ain & multiplexer_1_out;  // AND_Gate and_4, 8 bits wide
  assign or_1_out = Ain | multiplexer_1_out;  // OR_Gate or_1, 8 bits wide
  assign not_2_out = ~Ain;  // NOT_Gate not_2, 8 bits wide
  assign xor_1_out = Ain ^ multiplexer_1_out;  // XOR_Gate xor_1, 8 bits wide
  Comparator comparator_1 (.a(Ain), .b(multiplexer_1_out), .gt(Flags[3]), .eq(Flags[4]), .lt(Flags[5]));
  Multiplexer #(.select(4), .width(8)) multiplexer_2 (
    .in0(adder_1_out), .in1(subtractor_1_out), .in2(negator_1_out), .in3(shifter_1_out), .in4(shifter_2_out),
    .in5(and_4_out), .in6(or_1_out), .in7(not_2_out), .in8(xor_1_out), .in9(adder_1_out),
    .in10(subtractor_1_out), .in11({8{1'b0}}), .in12({8{1'b0}}), .in13({8{1'b0}}), .in14(adder_1_out),
    .in15(subtractor_1_out), .out({Flags[1], Sum[6:0]}), .sel(Cmd));
  or or_2 (Flags[0], adder_1_cout, subtractor_1_bout);
  assign not_3_out = ~{Flags[1], Sum[6:0]};  // NOT_Gate not_3, 8 bits wide
  and and_5 (Flags[2], not_3_out[0], not_3_out[1], not_3_out[2], not_3_out[3], not_3_out[4], not_3_out[5], not_3_out[6], not_3_out[7]);
  // Probe on Flags[1]
  // Probe on Flags[0]
  // Probe on Flags[3]
  // Probe on Flags[4]
  // Probe on Flags[5]
  // Probe on Flags[2]

  assign Flags[7:6] = 2'b00;
  assign Sum[7] = Flags[1];
endmodule

module cmdConv (
  input  [3:0] cmd,
  output [3:0] cmdOut
);

  wire and_1_out, and_2_out, and_3_out, and_4_out, and_5_out, and_6_out, not_1_out, not_2_out, not_3_out;

  not not_1 (not_1_out, cmd[3]);
  not not_2 (not_2_out, cmd[2]);
  not not_3 (not_3_out, cmd[1]);
  and and_1 (and_1_out, cmd[3], not_2_out);
  and and_2 (and_2_out, cmd[3], not_3_out);
  and and_3 (and_3_out, not_1_out, cmd[2]);
  and and_4 (and_4_out, cmd[2], not_3_out);
  and and_5 (and_5_out, not_1_out, cmd[1]);
  and and_6 (and_6_out, not_2_out, cmd[1]);
  or or_1 (cmdOut[3], and_1_out, and_2_out);
  or or_2 (cmdOut[2], and_3_out, and_4_out);
  or or_3 (cmdOut[1], and_5_out, and_6_out);

  assign cmdOut[0] = cmd[0];
endmodule
